# Fritzing sketch TeensyTyper (saved by Fritzing 0.7.6b)
breadboards: 1

parts:
  Teensy1 = Teensy 2.0
  DI1 = 7-Segment LED Display [package=THT]
  R1 = Resistor [tolerance=±5% resistance=1k package=THT]
  S3 = Pushbutton [package="[THT]"]
  S4 = Pushbutton [package="[THT]"]

nets:
  N1: Teensy1.GND, R1.Pin_0, S3.Pin_1, S3.Pin_2, S4.Pin_1, S4.Pin_2
  N2: Teensy1.B0, DI1.cathodeB
  N3: Teensy1.B1, DI1.cathodeA
  N4: Teensy1.B2, DI1.cathodeF
  N5: Teensy1.B3, DI1.cathodeG
  N6: Teensy1.D1, DI1.cathodeDP
  N7: Teensy1.D2, DI1.cathodeC
  N8: Teensy1.D3, DI1.cathodeD
  N9: Teensy1.C6, DI1.cathodeE
  N10: Teensy1.F4, S3.Pin_3, S3.Pin_4
  N11: Teensy1.F1, S4.Pin_3, S4.Pin_4
  N12: DI1.commAnode#7, R1.Pin_1
